// Logisim project Single Cycle Processor.circ as structural Verilog
module main (
  input  in_1
);

  wire ALUOp, ALUSrc, Clk, ExtOp, MemRd, MemWr, RegDst, REGWr, WBdata, Zero;
  wire [1:0] PCSrc;
  wire [2:0] multiplexer_2_out;
  wire [15:0] adder_1_out, adder_2_out, ALU_p4, bit_extender_1_out, bit_extender_2_out, File_Register_busa,
       File_Register_busb, multiplexer_1_out, multiplexer_3_out, multiplexer_4_out, multiplexer_5_out,
       ram_1_data, ram_2_data, register_1_q, undriven;

  Multiplexer #(.select(2), .width(16), .enable("false")) multiplexer_1 (
    .in0(adder_1_out), .in1(ram_1_data), .in2(adder_2_out), .in3(undriven), .out(multiplexer_1_out),
    .sel(PCSrc));
  Register #(.width(16)) register_1 (.D(multiplexer_1_out), .Q(register_1_q), .clk(Clk), .clr(in_1));  // open: en
  Adder #(.width(16)) adder_1 (.a(16'h1111), .b(register_1_q), .out(adder_1_out));  // open: cin, cout
  Clock clock_1 (.out(Clk));
  RAM #(.addrWidth(16), .dataWidth(16)) ram_1 (
    .addr(register_1_q), .data(ram_1_data), .clk(Clk), .ld(1'b1));  // open: sel, clr
  assign bit_extender_1_out = {{10{ram_1_data[15]}}, ram_1_data[15:10]};  // Bit_Extender bit_extender_1
  assign bit_extender_2_out = {{10{1'b0}}, ram_1_data[15:10]};  // Bit_Extender bit_extender_2
  Multiplexer #(.width(3), .enable("false")) multiplexer_2 (
    .in0(ram_1_data[9:7]), .in1(ram_1_data[12:10]), .out(multiplexer_2_out), .sel(RegDst));
  Multiplexer #(.width(16), .enable("false")) multiplexer_3 (
    .in0(bit_extender_1_out), .in1(bit_extender_2_out), .out(multiplexer_3_out), .sel(ExtOp));
  File_Register File_Register (
    .BusW(multiplexer_5_out), .RegWrite(REGWr), .RA(ram_1_data[6:4]), .RB(ram_1_data[9:7]),
    .BusA(File_Register_busa), .BusB(File_Register_busb), .RW(multiplexer_2_out), .Clock(Clk));
  Adder #(.width(16)) adder_2 (.a(adder_1_out), .b(multiplexer_3_out), .out(adder_2_out));  // open: cin, cout
  Multiplexer #(.width(16), .enable("false")) multiplexer_4 (
    .in0(File_Register_busb), .in1(multiplexer_3_out), .out(multiplexer_4_out), .sel(ALUSrc));
  // ALU ALU: pin names not known; wires that end beside it: File_Register_busa, multiplexer_4_out, ALUOp, ALU_p4, Zero
  RAM #(.addrWidth(16), .dataWidth(16), .bus("separate")) ram_2 (
    .addr(ALU_p4), .din(File_Register_busb), .data(ram_2_data), .str(MemRd), .clk(Clk), .ld(MemWr));  // open: sel, clr
  Multiplexer #(.width(16), .enable("false")) multiplexer_5 (
    .in0(ALU_p4), .in1(ram_2_data), .out(multiplexer_5_out), .sel(WBdata));
endmodule

module ALU (
  input  [1:0] Shift_Op,
  input  [15:0] A,
  input  Arithmetic_Op,
  input  [15:0] B,
  input  [1:0] Logical_Op,
  input  [1:0] ALU_Selection,
  output [15:0] ALU_result,
  output overflow,
  output zero
);

  wire xor_3_out;
  wire [15:0] adder_1_out, and_1_out, bit_extender_1_out, multiplexer_1_out, multiplexer_2_out, not_1_out,
       or_1_out, Shifter_data_out, xor_1_out, xor_2_out;

  Multiplexer #(.width(16), .enable("false")) multiplexer_1 (
    .in0({16{1'b0}}), .in1({16{1'b1}}), .out(multiplexer_1_out), .sel(Arithmetic_Op));
  assign xor_1_out = B ^ multiplexer_1_out;  // XOR_Gate xor_1, 16 bits wide
  assign and_1_out = A & B;  // AND_Gate and_1, 16 bits wide
  assign not_1_out = ~or_1_out;  // NOT_Gate not_1, 16 bits wide
  assign or_1_out = A | B;  // OR_Gate or_1, 16 bits wide
  assign xor_2_out = A ^ B;  // XOR_Gate xor_2, 16 bits wide
  Shifter Shifter (.Data(B), .Shift_amount(A[3:0]), .Shift_Op(Shift_Op), .Data_out(Shifter_data_out));
  Adder #(.width(16)) adder_1 (.a(A), .b(xor_1_out), .out(adder_1_out), .cin(Arithmetic_Op), .cout(overflow));
  Multiplexer #(.select(2), .width(16), .enable("false")) multiplexer_2 (
    .in0(and_1_out), .in1(or_1_out), .in2(not_1_out), .in3(xor_2_out), .out(multiplexer_2_out),
    .sel(Logical_Op));
  xor xor_3 (xor_3_out, adder_1_out[0], overflow);
  assign bit_extender_1_out = {{15{1'b0}}, xor_3_out};  // Bit_Extender bit_extender_1
  Multiplexer #(.select(2), .width(16), .enable("false")) multiplexer_3 (
    .in0(Shifter_data_out), .in1(bit_extender_1_out), .in2(adder_1_out), .in3(multiplexer_2_out),
    .out(ALU_result), .sel(ALU_Selection));
  nor nor_1 (zero, ALU_result[15], ALU_result[14], ALU_result[13], ALU_result[12], ALU_result[11], ALU_result[10], ALU_result[9], ALU_result[8], ALU_result[6], ALU_result[5], ALU_result[4], ALU_result[3], ALU_result[2], ALU_result[1], ALU_result[0], ALU_result[7]);
endmodule

module Shifter (
  input  [15:0] Data,
  input  [3:0] Shift_amount,
  input  [1:0] Shift_Op,
  output [15:0] Data_out
);

  wire [15:0] shifter_1_out, shifter_2_out, shifter_3_out, shifter_4_out;

  Shifter_part #(.width(16)) shifter_1 (.in(Data), .\dist (Shift_amount), .out(shifter_1_out));
  Shifter_part #(.width(16), .shift("lr")) shifter_2 (.in(Data), .\dist (Shift_amount), .out(shifter_2_out));
  Shifter_part #(.width(16), .shift("ar")) shifter_3 (.in(Data), .\dist (Shift_amount), .out(shifter_3_out));
  Shifter_part #(.width(16), .shift("rr")) shifter_4 (.in(Data), .\dist (Shift_amount), .out(shifter_4_out));
  Multiplexer #(.select(2), .width(16), .enable("false")) multiplexer_1 (
    .in0(shifter_1_out), .in1(shifter_2_out), .in2(shifter_3_out), .in3(shifter_4_out), .out(Data_out),
    .sel(Shift_Op));
endmodule

module File_Register (
  input  [2:0] RA,
  input  [2:0] RB,
  input  [2:0] RW,
  input  [15:0] BusW,
  input  RegWrite,
  input  Clock,
  output [15:0] BusA,
  output [15:0] BusB
);

  wire and_1_out, and_2_out, and_3_out, and_4_out, and_5_out, and_6_out, and_7_out, decoder_1_out0,
       decoder_1_out1, decoder_1_out2, decoder_1_out3, decoder_1_out4, decoder_1_out5, decoder_1_out6,
       decoder_1_out7, decoder_2_out0, decoder_2_out1, decoder_2_out2, decoder_2_out3, decoder_2_out4,
       decoder_2_out5, decoder_2_out6, decoder_2_out7, decoder_3_out0, decoder_3_out1, decoder_3_out2,
       decoder_3_out3, decoder_3_out4, decoder_3_out5, decoder_3_out6, decoder_3_out7;
  wire [15:0] R1_q, R2_q, R3_q, R4_q, R5_q, R6_q;

  Decoder #(.select(3), .enable("false")) decoder_1 (
    .out0(decoder_1_out0), .out1(decoder_1_out1), .out2(decoder_1_out2), .out3(decoder_1_out3),
    .out4(decoder_1_out4), .out5(decoder_1_out5), .out6(decoder_1_out6), .out7(decoder_1_out7), .sel(RW));
  Register #(.width(16)) R1 (.D(BusW), .en(and_1_out), .Q(R1_q), .clk(Clock));  // open: clr
  and and_1 (and_1_out, decoder_1_out1, RegWrite);
  Register #(.width(16)) R2 (.D(BusW), .en(and_2_out), .Q(R2_q), .clk(Clock));  // open: clr
  and and_2 (and_2_out, decoder_1_out2, RegWrite);
  Register #(.width(16)) R3 (.D(BusW), .en(and_3_out), .Q(R3_q), .clk(Clock));  // open: clr
  and and_3 (and_3_out, decoder_1_out3, RegWrite);
  Register #(.width(16)) R4 (.D(BusW), .en(and_4_out), .Q(R4_q), .clk(Clock));  // open: clr
  and and_4 (and_4_out, decoder_1_out4, RegWrite);
  Register #(.width(16)) R5 (.D(BusW), .en(and_5_out), .Q(R5_q), .clk(Clock));  // open: clr
  and and_5 (and_5_out, decoder_1_out5, RegWrite);
  Register #(.width(16)) R6 (.D(BusW), .en(and_6_out), .Q(R6_q), .clk(Clock));  // open: clr
  and and_6 (and_6_out, decoder_1_out6, RegWrite);
  Register #(.width(16)) R7 (.D(BusW), .en(and_7_out), .Q(BusA), .clk(Clock));  // open: clr
  and and_7 (and_7_out, decoder_1_out7, RegWrite);
  Decoder #(.select(3), .enable("false")) decoder_2 (
    .out0(decoder_2_out0), .out1(decoder_2_out1), .out2(decoder_2_out2), .out3(decoder_2_out3),
    .out4(decoder_2_out4), .out5(decoder_2_out5), .out6(decoder_2_out6), .out7(decoder_2_out7), .sel(RA));
  assign BusA = decoder_2_out1 ? R1_q : 16'bz;  // Controlled_Buffer controlled_buffer_1
  assign BusA = decoder_2_out2 ? R2_q : 16'bz;  // Controlled_Buffer controlled_buffer_2
  assign BusA = decoder_2_out3 ? R3_q : 16'bz;  // Controlled_Buffer controlled_buffer_3
  assign BusA = decoder_2_out4 ? R4_q : 16'bz;  // Controlled_Buffer controlled_buffer_4
  assign BusA = decoder_2_out5 ? R5_q : 16'bz;  // Controlled_Buffer controlled_buffer_5
  assign BusA = decoder_2_out6 ? R6_q : 16'bz;  // Controlled_Buffer controlled_buffer_6
  assign BusA = decoder_2_out7 ? BusA : 16'bz;  // Controlled_Buffer controlled_buffer_7
  assign BusA = decoder_2_out0 ? {16{1'b0}} : 16'bz;  // Controlled_Buffer controlled_buffer_8
  Decoder #(.select(3), .enable("false")) decoder_3 (
    .out0(decoder_3_out0), .out1(decoder_3_out1), .out2(decoder_3_out2), .out3(decoder_3_out3),
    .out4(decoder_3_out4), .out5(decoder_3_out5), .out6(decoder_3_out6), .out7(decoder_3_out7), .sel(RB));
  assign BusB = decoder_3_out0 ? {16{1'b0}} : 16'bz;  // Controlled_Buffer controlled_buffer_9
  assign BusB = decoder_3_out1 ? R1_q : 16'bz;  // Controlled_Buffer controlled_buffer_10
  assign BusB = decoder_3_out2 ? R2_q : 16'bz;  // Controlled_Buffer controlled_buffer_11
  assign BusB = decoder_3_out3 ? R3_q : 16'bz;  // Controlled_Buffer controlled_buffer_12
  assign BusB = decoder_3_out4 ? R4_q : 16'bz;  // Controlled_Buffer controlled_buffer_13
  assign BusB = decoder_3_out5 ? R5_q : 16'bz;  // Controlled_Buffer controlled_buffer_14
  assign BusB = decoder_3_out6 ? R6_q : 16'bz;  // Controlled_Buffer controlled_buffer_15
  assign BusB = decoder_3_out7 ? BusA : 16'bz;  // Controlled_Buffer controlled_buffer_16
endmodule
